// Logisim project ram.circ as structural Verilog: 8 circuits, main circuit main
module main (
);

  register_file register_file_1 ();  // open: src1, src2, dest, inData, WriteEnable, clock, outdata1, outdata2
endmodule

module _1_bit_register (
  input  \input ,
  input  eneable,
  input  clock,
  output \output 
);

  wire multiplexer_1_out;

  Multiplexer #(.enable("false")) multiplexer_1 (.in0(\output ), .in1(\input ), .out(multiplexer_1_out), .sel(eneable));
  d_latch d_latch_1 (.\input (multiplexer_1_out), .clock(clock), .Q(\output ));
endmodule

module d_latch (
  input  \input ,
  input  clock,
  output Q
);

  wire and_1_out, and_2_out, nor_1_out, not_1_out;

  not not_1 (not_1_out, \input );
  and and_1 (and_1_out, \input , clock);
  and and_2 (and_2_out, clock, not_1_out);
  nor nor_1 (nor_1_out, and_1_out, Q);
  nor nor_2 (Q, nor_1_out, and_2_out);
endmodule

module flip_flop (
  input  \input ,
  input  clock,
  output Q
);

  wire d_latch_1_q, not_1_out;

  d_latch d_latch_1 (.\input (\input ), .clock(clock), .Q(d_latch_1_q));
  not not_1 (not_1_out, clock);
  d_latch d_latch_2 (.\input (d_latch_1_q), .clock(not_1_out), .Q(Q));
endmodule

module _18_bit_register (
  input  [17:0] \input ,
  input  enable,
  input  clock,
  output [17:0] \output 
);

  _1_bit_register u_1_bit_register_1 (.\input (\input [0]), .eneable(enable), .clock(clock), .\output (\output [0]));
  _1_bit_register u_1_bit_register_2 (.\input (\input [1]), .eneable(enable), .clock(clock), .\output (\output [1]));
  _1_bit_register u_1_bit_register_3 (.\input (\input [2]), .eneable(enable), .clock(clock), .\output (\output [2]));
  _1_bit_register u_1_bit_register_4 (.\input (\input [3]), .eneable(enable), .clock(clock), .\output (\output [3]));
  _1_bit_register u_1_bit_register_5 (.\input (\input [4]), .eneable(enable), .clock(clock), .\output (\output [4]));
  _1_bit_register u_1_bit_register_6 (.\input (\input [6]), .eneable(enable), .clock(clock), .\output (\output [6]));
  _1_bit_register u_1_bit_register_7 (.\input (\input [5]), .eneable(enable), .clock(clock), .\output (\output [5]));
  _1_bit_register u_1_bit_register_8 (.\input (\input [7]), .eneable(enable), .clock(clock), .\output (\output [7]));
  _1_bit_register u_1_bit_register_9 (.\input (\input [8]), .eneable(enable), .clock(clock), .\output (\output [8]));
  _1_bit_register u_1_bit_register_10 (.\input (\input [9]), .eneable(enable), .clock(clock), .\output (\output [9]));
  _1_bit_register u_1_bit_register_11 (.\input (\input [10]), .eneable(enable), .clock(clock), .\output (\output [10]));
  _1_bit_register u_1_bit_register_12 (.\input (\input [11]), .eneable(enable), .clock(clock), .\output (\output [11]));
  _1_bit_register u_1_bit_register_13 (.\input (\input [12]), .eneable(enable), .clock(clock), .\output (\output [12]));
  _1_bit_register u_1_bit_register_14 (.\input (\input [14]), .eneable(enable), .clock(clock), .\output (\output [14]));
  _1_bit_register u_1_bit_register_15 (.\input (\input [13]), .eneable(enable), .clock(clock), .\output (\output [13]));
  _1_bit_register u_1_bit_register_16 (.\input (\input [15]), .eneable(enable), .clock(clock), .\output (\output [15]));
  _1_bit_register u_1_bit_register_17 (.\input (\input [16]), .eneable(enable), .clock(clock), .\output (\output [16]));
  _1_bit_register u_1_bit_register_18 (.\input (\input [17]), .eneable(enable), .clock(clock), .\output (\output [17]));
endmodule

module register_file (
  input  [3:0] src1,
  input  [3:0] src2,
  input  [3:0] dest,
  input  [17:0] inData,
  input  WriteEnable,
  input  clock,
  output [17:0] outdata1,
  output [17:0] outdata2
);

  wire and_1_out, and_2_out, and_3_out, and_4_out, and_5_out, and_6_out, and_7_out, and_8_out, and_9_out,
       and_10_out, and_11_out, and_12_out, and_13_out, and_14_out, and_15_out, and_16_out, decoder_1_out0,
       decoder_1_out1, decoder_1_out2, decoder_1_out3, decoder_1_out4, decoder_1_out5, decoder_1_out6,
       decoder_1_out7, decoder_1_out8, decoder_1_out9, decoder_1_out10, decoder_1_out11, decoder_1_out12,
       decoder_1_out13, decoder_1_out14, decoder_1_out15, decoder_2_out0, decoder_2_out1, decoder_2_out2,
       decoder_2_out3, decoder_2_out4, decoder_2_out5, decoder_2_out6, decoder_2_out7, decoder_2_out8,
       decoder_2_out9, decoder_2_out10, decoder_2_out11, decoder_2_out12, decoder_2_out13, decoder_2_out14,
       decoder_2_out15, decoder_3_out0, decoder_3_out1, decoder_3_out2, decoder_3_out3, decoder_3_out4,
       decoder_3_out5, decoder_3_out6, decoder_3_out7, decoder_3_out8, decoder_3_out9, decoder_3_out10,
       decoder_3_out11, decoder_3_out12, decoder_3_out13, decoder_3_out14, decoder_3_out15;
  wire [17:0] n18_bit_register_1_output, n18_bit_register_2_output, n18_bit_register_3_output,
       n18_bit_register_4_output, n18_bit_register_5_output, n18_bit_register_6_output,
       n18_bit_register_7_output, n18_bit_register_8_output, n18_bit_register_9_output,
       n18_bit_register_10_output, n18_bit_register_11_output, n18_bit_register_12_output,
       n18_bit_register_13_output, n18_bit_register_14_output, n18_bit_register_15_output,
       n18_bit_register_16_output;

  Decoder #(.select(4), .enable("false")) decoder_1 (
    .out0(decoder_1_out0), .out1(decoder_1_out1), .out2(decoder_1_out2), .out3(decoder_1_out3),
    .out4(decoder_1_out4), .out5(decoder_1_out5), .out6(decoder_1_out6), .out7(decoder_1_out7),
    .out8(decoder_1_out8), .out9(decoder_1_out9), .out10(decoder_1_out10), .out11(decoder_1_out11),
    .out12(decoder_1_out12), .out13(decoder_1_out13), .out14(decoder_1_out14), .out15(decoder_1_out15),
    .sel(src1));
  Decoder #(.select(4), .enable("false")) decoder_2 (
    .out0(decoder_2_out0), .out1(decoder_2_out1), .out2(decoder_2_out2), .out3(decoder_2_out3),
    .out4(decoder_2_out4), .out5(decoder_2_out5), .out6(decoder_2_out6), .out7(decoder_2_out7),
    .out8(decoder_2_out8), .out9(decoder_2_out9), .out10(decoder_2_out10), .out11(decoder_2_out11),
    .out12(decoder_2_out12), .out13(decoder_2_out13), .out14(decoder_2_out14), .out15(decoder_2_out15),
    .sel(src2));
  _1_bir_alu u_1_bir_alu_1 ();  // open: result, oparand1, operand2, carryIn, operation, carryOut
  Decoder #(.select(4), .enable("false")) decoder_3 (
    .out0(decoder_3_out0), .out1(decoder_3_out1), .out2(decoder_3_out2), .out3(decoder_3_out3),
    .out4(decoder_3_out4), .out5(decoder_3_out5), .out6(decoder_3_out6), .out7(decoder_3_out7),
    .out8(decoder_3_out8), .out9(decoder_3_out9), .out10(decoder_3_out10), .out11(decoder_3_out11),
    .out12(decoder_3_out12), .out13(decoder_3_out13), .out14(decoder_3_out14), .out15(decoder_3_out15),
    .sel(dest));
  _18_bit_register u_18_bit_register_1 (
    .\input (inData), .enable(and_1_out), .clock(clock), .\output (n18_bit_register_1_output));
  and and_1 (and_1_out, decoder_3_out0, WriteEnable);
  _18_bit_register u_18_bit_register_2 (
    .\input (inData), .enable(and_2_out), .clock(clock), .\output (n18_bit_register_2_output));
  and and_2 (and_2_out, decoder_3_out1, WriteEnable);
  _18_bit_register u_18_bit_register_3 (
    .\input (inData), .enable(and_3_out), .clock(clock), .\output (n18_bit_register_3_output));
  and and_3 (and_3_out, decoder_3_out2, WriteEnable);
  _18_bit_register u_18_bit_register_4 (
    .\input (inData), .enable(and_4_out), .clock(clock), .\output (n18_bit_register_4_output));
  and and_4 (and_4_out, decoder_3_out3, WriteEnable);
  _18_bit_register u_18_bit_register_5 (
    .\input (inData), .enable(and_5_out), .clock(clock), .\output (n18_bit_register_5_output));
  and and_5 (and_5_out, decoder_3_out4, WriteEnable);
  _18_bit_register u_18_bit_register_6 (
    .\input (inData), .enable(and_6_out), .clock(clock), .\output (n18_bit_register_6_output));
  and and_6 (and_6_out, decoder_3_out5, WriteEnable);
  _18_bit_register u_18_bit_register_7 (
    .\input (inData), .enable(and_7_out), .clock(clock), .\output (n18_bit_register_7_output));
  and and_7 (and_7_out, decoder_3_out6, WriteEnable);
  _18_bit_register u_18_bit_register_8 (
    .\input (inData), .enable(and_8_out), .clock(clock), .\output (n18_bit_register_8_output));
  and and_8 (and_8_out, decoder_3_out7, WriteEnable);
  _18_bit_register u_18_bit_register_9 (
    .\input (inData), .enable(and_9_out), .clock(clock), .\output (n18_bit_register_9_output));
  and and_9 (and_9_out, decoder_3_out8, WriteEnable);
  _18_bit_register u_18_bit_register_10 (
    .\input (inData), .enable(and_10_out), .clock(clock), .\output (n18_bit_register_10_output));
  buf and_10 (and_10_out, decoder_3_out9);  // AND_Gate
  _18_bit_register u_18_bit_register_11 (
    .\input (inData), .enable(and_11_out), .clock(clock), .\output (n18_bit_register_11_output));
  and and_11 (and_11_out, decoder_3_out10, WriteEnable);
  _18_bit_register u_18_bit_register_12 (
    .\input (inData), .enable(and_12_out), .clock(clock), .\output (n18_bit_register_12_output));
  and and_12 (and_12_out, decoder_3_out11, WriteEnable);
  _18_bit_register u_18_bit_register_13 (
    .\input (inData), .enable(and_13_out), .clock(clock), .\output (n18_bit_register_13_output));
  and and_13 (and_13_out, decoder_3_out12, WriteEnable);
  _18_bit_register u_18_bit_register_14 (
    .\input (inData), .enable(and_14_out), .clock(clock), .\output (n18_bit_register_14_output));
  and and_14 (and_14_out, decoder_3_out13, WriteEnable);
  _18_bit_register u_18_bit_register_15 (
    .\input (inData), .enable(and_15_out), .clock(clock), .\output (n18_bit_register_15_output));
  and and_15 (and_15_out, decoder_3_out14, WriteEnable);
  _18_bit_register u_18_bit_register_16 (
    .\input (inData), .enable(and_16_out), .clock(clock), .\output (n18_bit_register_16_output));
  and and_16 (and_16_out, decoder_3_out15, WriteEnable);
  assign outdata1 = decoder_1_out0 ? n18_bit_register_1_output : 18'bz;  // Controlled_Buffer controlled_buffer_1
  assign outdata2 = decoder_2_out0 ? n18_bit_register_1_output : 18'bz;  // Controlled_Buffer controlled_buffer_2
  assign outdata1 = decoder_1_out1 ? n18_bit_register_2_output : 18'bz;  // Controlled_Buffer controlled_buffer_3
  assign outdata2 = decoder_2_out1 ? n18_bit_register_2_output : 18'bz;  // Controlled_Buffer controlled_buffer_4
  assign outdata1 = decoder_1_out2 ? n18_bit_register_3_output : 18'bz;  // Controlled_Buffer controlled_buffer_5
  assign outdata2 = decoder_2_out2 ? n18_bit_register_3_output : 18'bz;  // Controlled_Buffer controlled_buffer_6
  assign outdata1 = decoder_1_out3 ? n18_bit_register_4_output : 18'bz;  // Controlled_Buffer controlled_buffer_7
  assign outdata2 = decoder_2_out3 ? n18_bit_register_4_output : 18'bz;  // Controlled_Buffer controlled_buffer_8
  assign outdata1 = decoder_1_out4 ? n18_bit_register_5_output : 18'bz;  // Controlled_Buffer controlled_buffer_9
  assign outdata2 = decoder_2_out4 ? n18_bit_register_5_output : 18'bz;  // Controlled_Buffer controlled_buffer_10
  assign outdata1 = decoder_1_out5 ? n18_bit_register_6_output : 18'bz;  // Controlled_Buffer controlled_buffer_11
  assign outdata2 = decoder_2_out5 ? n18_bit_register_6_output : 18'bz;  // Controlled_Buffer controlled_buffer_12
  assign outdata1 = decoder_1_out6 ? n18_bit_register_7_output : 18'bz;  // Controlled_Buffer controlled_buffer_13
  assign outdata2 = decoder_2_out6 ? n18_bit_register_7_output : 18'bz;  // Controlled_Buffer controlled_buffer_14
  assign outdata1 = decoder_1_out7 ? n18_bit_register_8_output : 18'bz;  // Controlled_Buffer controlled_buffer_15
  assign outdata2 = decoder_2_out7 ? n18_bit_register_8_output : 18'bz;  // Controlled_Buffer controlled_buffer_16
  assign outdata1 = decoder_1_out8 ? n18_bit_register_9_output : 18'bz;  // Controlled_Buffer controlled_buffer_17
  assign outdata2 = decoder_2_out8 ? n18_bit_register_9_output : 18'bz;  // Controlled_Buffer controlled_buffer_18
  assign outdata1 = decoder_1_out9 ? n18_bit_register_10_output : 18'bz;  // Controlled_Buffer controlled_buffer_19
  assign outdata2 = decoder_2_out9 ? n18_bit_register_10_output : 18'bz;  // Controlled_Buffer controlled_buffer_20
  assign outdata1 = decoder_1_out10 ? n18_bit_register_11_output : 18'bz;  // Controlled_Buffer controlled_buffer_21
  assign outdata2 = decoder_2_out10 ? n18_bit_register_11_output : 18'bz;  // Controlled_Buffer controlled_buffer_22
  assign outdata1 = decoder_1_out11 ? n18_bit_register_12_output : 18'bz;  // Controlled_Buffer controlled_buffer_23
  assign outdata2 = decoder_2_out11 ? n18_bit_register_12_output : 18'bz;  // Controlled_Buffer controlled_buffer_24
  assign outdata1 = decoder_1_out12 ? n18_bit_register_13_output : 18'bz;  // Controlled_Buffer controlled_buffer_25
  assign outdata2 = decoder_2_out12 ? n18_bit_register_13_output : 18'bz;  // Controlled_Buffer controlled_buffer_26
  assign outdata1 = decoder_1_out13 ? n18_bit_register_14_output : 18'bz;  // Controlled_Buffer controlled_buffer_27
  assign outdata2 = decoder_2_out13 ? n18_bit_register_14_output : 18'bz;  // Controlled_Buffer controlled_buffer_28
  assign outdata1 = decoder_1_out14 ? n18_bit_register_15_output : 18'bz;  // Controlled_Buffer controlled_buffer_29
  assign outdata2 = decoder_2_out14 ? n18_bit_register_15_output : 18'bz;  // Controlled_Buffer controlled_buffer_30
  assign outdata1 = decoder_1_out15 ? n18_bit_register_16_output : 18'bz;  // Controlled_Buffer controlled_buffer_31
  assign outdata2 = decoder_2_out15 ? n18_bit_register_16_output : 18'bz;  // Controlled_Buffer controlled_buffer_32
endmodule

module _1_bir_alu (
  input  carryIn,
  input  oparand1,
  input  operand2,
  input  [1:0] operation,
  output carryOut,
  output result
);

  wire adder_1_out, and_1_out, or_1_out, xor_1_out;

  and and_1 (and_1_out, operand2, oparand1);
  or or_1 (or_1_out, operand2, oparand1);
  xor xor_1 (xor_1_out, operand2, oparand1);
  Adder #(.width(1)) adder_1 (.a(operand2), .b(oparand1), .out(adder_1_out), .cin(carryIn), .cout(carryOut));
  Multiplexer #(.select(2), .enable("false")) multiplexer_1 (
    .in0(and_1_out), .in1(or_1_out), .in2(xor_1_out), .in3(adder_1_out), .out(result), .sel(operation));
endmodule

module _18bitALU (
  input  Carry_In,
  input  [17:0] Operand_A,
  input  [17:0] Operand_B,
  input  [1:0] Operation,
  output [17:0] out_5,
  output overflow
);

  wire n1_bir_alu_1_carryout, n1_bir_alu_2_carryout, n1_bir_alu_3_carryout, n1_bir_alu_4_carryout,
       n1_bir_alu_5_carryout, n1_bir_alu_6_carryout, n1_bir_alu_7_carryout, n1_bir_alu_8_carryout,
       n1_bir_alu_9_carryout, n1_bir_alu_10_carryout, n1_bir_alu_11_carryout, n1_bir_alu_12_carryout,
       n1_bir_alu_13_carryout, n1_bir_alu_14_carryout, n1_bir_alu_15_carryout, n1_bir_alu_16_carryout,
       n1_bir_alu_17_carryout;

  _1_bir_alu u_1_bir_alu_1 (
    .result(out_5[0]), .oparand1(Operand_A[0]), .operand2(Operand_B[0]), .carryIn(Carry_In),
    .operation(Operation), .carryOut(n1_bir_alu_1_carryout));
  _1_bir_alu u_1_bir_alu_2 (
    .result(out_5[1]), .oparand1(Operand_A[1]), .operand2(Operand_B[1]), .carryIn(n1_bir_alu_1_carryout),
    .operation(Operation), .carryOut(n1_bir_alu_2_carryout));
  _1_bir_alu u_1_bir_alu_3 (
    .result(out_5[2]), .oparand1(Operand_A[2]), .operand2(Operand_B[2]), .carryIn(n1_bir_alu_2_carryout),
    .operation(Operation), .carryOut(n1_bir_alu_3_carryout));
  _1_bir_alu u_1_bir_alu_4 (
    .result(out_5[3]), .oparand1(Operand_A[3]), .operand2(Operand_B[3]), .carryIn(n1_bir_alu_3_carryout),
    .operation(Operation), .carryOut(n1_bir_alu_4_carryout));
  _1_bir_alu u_1_bir_alu_5 (
    .result(out_5[4]), .oparand1(Operand_A[4]), .operand2(Operand_B[4]), .carryIn(n1_bir_alu_4_carryout),
    .operation(Operation), .carryOut(n1_bir_alu_5_carryout));
  _1_bir_alu u_1_bir_alu_6 (
    .result(out_5[5]), .oparand1(Operand_A[5]), .operand2(Operand_B[5]), .carryIn(n1_bir_alu_5_carryout),
    .operation(Operation), .carryOut(n1_bir_alu_6_carryout));
  _1_bir_alu u_1_bir_alu_7 (
    .result(out_5[6]), .oparand1(Operand_A[6]), .operand2(Operand_B[6]), .carryIn(n1_bir_alu_6_carryout),
    .operation(Operation), .carryOut(n1_bir_alu_7_carryout));
  _1_bir_alu u_1_bir_alu_8 (
    .result(out_5[7]), .oparand1(Operand_A[7]), .operand2(Operand_B[7]), .carryIn(n1_bir_alu_7_carryout),
    .operation(Operation), .carryOut(n1_bir_alu_8_carryout));
  _1_bir_alu u_1_bir_alu_9 (
    .result(out_5[8]), .oparand1(Operand_A[8]), .operand2(Operand_B[8]), .carryIn(n1_bir_alu_8_carryout),
    .operation(Operation), .carryOut(n1_bir_alu_9_carryout));
  _1_bir_alu u_1_bir_alu_10 (
    .result(out_5[9]), .oparand1(Operand_A[9]), .operand2(Operand_B[9]), .carryIn(n1_bir_alu_9_carryout),
    .operation(Operation), .carryOut(n1_bir_alu_10_carryout));
  _1_bir_alu u_1_bir_alu_11 (
    .result(out_5[10]), .oparand1(Operand_A[10]), .operand2(Operand_B[10]), .carryIn(n1_bir_alu_10_carryout),
    .operation(Operation), .carryOut(n1_bir_alu_11_carryout));
  _1_bir_alu u_1_bir_alu_12 (
    .result(out_5[11]), .oparand1(Operand_A[11]), .operand2(Operand_B[11]), .carryIn(n1_bir_alu_11_carryout),
    .operation(Operation), .carryOut(n1_bir_alu_12_carryout));
  _1_bir_alu u_1_bir_alu_13 (
    .result(out_5[12]), .oparand1(Operand_A[12]), .operand2(Operand_B[12]), .carryIn(n1_bir_alu_12_carryout),
    .operation(Operation), .carryOut(n1_bir_alu_13_carryout));
  _1_bir_alu u_1_bir_alu_14 (
    .result(out_5[13]), .oparand1(Operand_A[13]), .operand2(Operand_B[13]), .carryIn(n1_bir_alu_13_carryout),
    .operation(Operation), .carryOut(n1_bir_alu_14_carryout));
  _1_bir_alu u_1_bir_alu_15 (
    .result(out_5[14]), .oparand1(Operand_A[14]), .operand2(Operand_B[14]), .carryIn(n1_bir_alu_14_carryout),
    .operation(Operation), .carryOut(n1_bir_alu_15_carryout));
  _1_bir_alu u_1_bir_alu_16 (
    .result(out_5[15]), .oparand1(Operand_A[15]), .operand2(Operand_B[15]), .carryIn(n1_bir_alu_15_carryout),
    .operation(Operation), .carryOut(n1_bir_alu_16_carryout));
  _1_bir_alu u_1_bir_alu_17 (
    .result(out_5[16]), .oparand1(Operand_A[16]), .operand2(Operand_B[16]), .carryIn(n1_bir_alu_16_carryout),
    .operation(Operation), .carryOut(n1_bir_alu_17_carryout));
  _1_bir_alu u_1_bir_alu_18 (
    .result(out_5[17]), .oparand1(Operand_A[17]), .operand2(Operand_B[17]), .carryIn(n1_bir_alu_17_carryout),
    .operation(Operation), .carryOut(overflow));

  // Other names for the same wires on the sheet: A0 = Operand_A[0]; A1 = Operand_A[1]; A2 = Operand_A[2];
  //   A3 = Operand_A[3]; A4 = Operand_A[4]; A5 = Operand_A[5]; A6 = Operand_A[6]; A7 = Operand_A[7];
  //   A8 = Operand_A[8]; A9 = Operand_A[9]; A10 = Operand_A[10]; A11 = Operand_A[11]; A12 = Operand_A[12];
  //   A13 = Operand_A[13]; A14 = Operand_A[14]; A15 = Operand_A[15]; A16 = Operand_A[16]; A17 = Operand_A[17];
  //   B0 = Operand_B[0]; B1 = Operand_B[1]; B2 = Operand_B[2]; B3 = Operand_B[3]; B4 = Operand_B[4];
  //   B5 = Operand_B[5]; B6 = Operand_B[6]; B7 = Operand_B[7]; B8 = Operand_B[8]; B9 = Operand_B[9];
  //   B10 = Operand_B[10]; B11 = Operand_B[11]; B12 = Operand_B[12]; B13 = Operand_B[13]; B14 = Operand_B[14];
  //   B15 = Operand_B[15]; B16 = Operand_B[16]; B17 = Operand_B[17]
endmodule
